# Fritzing sketch Jetta_Brain (saved by Fritzing 1.0.1rc)

parts:
  F1 = FUSE [package=fuse_5mm]
  F2 = FUSE [package=fuse_5mm]
  F3 = FUSE [package=fuse_5mm]
  F4 = FUSE [package=fuse_5mm]
  F6 = FUSE [package=fuse_5mm]
  F5 = FUSE [package=fuse_5mm]
  U1 = RELAY [package=relay-g5q]
  LED1 = LEDs [package=led-1206]
  Part1 = Arduino Nano (Rev3.0)
  V2 = DC Power [voltage=5]

nets:
  N1: F1.1, U1.MAIN
  12V: F1.2, F2.2, F3.2, F4.1, F6.1, F5.1, V2.V+
  N2: U1.COIL2, Part1.D2
  N3: U1.NO, LED1.A
  GND: LED1.C, V2.V-
